# Fritzing sketch Diagram (saved by Fritzing 0.9.2b)

parts:
  ArduinoUnoBarrelJack12v = Arduino Uno (Rev3) - ICSP
  PiezoSpeaker = Piezo Speaker
  part = TRANSISTOR_NPN_2 [package=to-92]
  part_2 = Resistor [resistance=1k package=THT]
  PIR = PIR sensor
  part_3 = Resistor [resistance=10k package=THT]

nets:
  N1: ArduinoUnoBarrelJack12v.D2, PIR.SIG, part_3.Pin_0
  N2: ArduinoUnoBarrelJack12v.D3_PWM, part_2.Pin_0
  N3: ArduinoUnoBarrelJack12v.5V, PiezoSpeaker.pin2
  GND: ArduinoUnoBarrelJack12v.GND, part.E, PIR.GND
  VIN: ArduinoUnoBarrelJack12v.VIN, PIR.VCC, part_3.Pin_1
  N4: PiezoSpeaker.pin1, part.C
  N5: part.B, part_2.Pin_1

custom parts:
  TRANSISTOR_NPN_2: Alternate TO-92 NPN BJT
